# Fritzing sketch cabling (saved by Fritzing 0.9.3b)
breadboards: 1

parts:
  Composant1 = Arduino Nano (Rev3.0)
  Composant2 = Thumb Joystick
  J5 = Basic Servo
  J2 = Basic Servo
  J4 = Basic Servo
  J3 = Basic Servo
  Composant3 = Thumb Joystick
  Power_plug1 = Power plug

nets:
  GND: Composant1.GND, Composant2.GND, J5.gnd, J2.gnd, J4.gnd, J3.gnd, Composant3.GND, Power_plug1.GND
  N1: Composant1.D6, J5.pulse
  N2: Composant1.D9, J4.pulse
  N3: Composant1.D10, J3.pulse
  N4: Composant1.D11/MOSI, J2.pulse
  VCC: Composant1.5V, Composant2.VCC, J5.vcc, J2.vcc, J4.vcc, J3.vcc, Composant3.VCC, Power_plug1.VCC
  N5: Composant1.A3, Composant2.HORZ
  N6: Composant1.A2, Composant3.HORZ
  N7: Composant1.A1, Composant2.VERT
  N8: Composant1.A0, Composant3.VERT

notes:
  middle
  left
  right
  claw
